// Logisim project DDCA LOGISM PROJECT.circ as structural Verilog: 1 circuit, main circuit main
module main (
  input  A,
  input  W,
  input  B,
  input  X,
  input  C,
  input  Y,
  input  D,
  input  Z,
  output ACCESS
);

  wire XNOR_2_out, XNOR_3_out, XNOR_4_out, XNOR_out;

  xnor XNOR (XNOR_out, A, W);
  xnor XNOR_2 (XNOR_2_out, B, X);
  xnor XNOR_3 (XNOR_3_out, C, Y);
  xnor XNOR_4 (XNOR_4_out, D, Z);
  and AND (ACCESS, XNOR_out, XNOR_2_out, XNOR_3_out, XNOR_4_out);
endmodule
